# Fritzing sketch joystick_down (saved by Fritzing 0.9.3b)
circuit board: 5.80057cm x 3.01508cm
breadboards: 1

parts:
  Part2 = Arduino Nano (Rev3.0)
  J1 = female pin header, 15 pins [form="♀ (female)"]
  J2 = female pin header, 15 pins [form="♀ (female)"]
  Joystick_Right = female pin header, 5 pins [form="♀ (female)"]
  Joystick_Left = female pin header, 5 pins [form="♀ (female)"]
  Joystick_Left2 = female pin header, 3 pins [form="♀ (female)"]
  Joystick_Left3 = female pin header, 2 pins [form="♀ (female)"]
  Joystick_Left1 = female pin header, 5 pins [form="♀ (female)"]
  Joystick_Left4 = female pin header, 1 pin [form="♀ (female)"]
  Joystick_Left5 = female pin header, 2 pins [form="♀ (female)"]
  Joystick_Left6 = female pin header, 1 pin [form="♀ (female)"]
  Joystick_Left7 = female pin header, 1 pin [form="♀ (female)"]
  Joystick_Left8 = female pin header, 1 pin [form="♀ (female)"]
  Joystick_Left9 = female pin header, 1 pin [form="♀ (female)"]
  Joystick_Left10 = female pin header, 1 pin [form="♀ (female)"]
  Joystick_Left11 = female pin header, 1 pin [form="♀ (female)"]
  Joystick_Left12 = female pin header, 1 pin [form="♀ (female)"]
  Joystick_Left13 = female pin header, 1 pin [form="♀ (female)"]
  Joystick_Left14 = female pin header, 1 pin [form="♀ (female)"]
  Joystick_Left15 = female pin header, 1 pin [form="♀ (female)"]
  R1 = Resistor [tolerance=±5% resistance=2.2k package=THT]
  R2 = Resistor [tolerance=±5% resistance=4.7k package=THT]

nets:
  N1: Part2.D1/TX, J2.pin1
  N2: Part2.D0/RX, J2.pin2
  N3: Part2.RESET, J1.pin3, J2.pin3
  N4: Part2.GND, J1.pin2, J2.pin4, Joystick_Right.pin5, Joystick_Left.pin1, Joystick_Left3.pin2, Joystick_Left1.pin1, Joystick_Left4.pin1, Joystick_Left5.pin2, Joystick_Left15.pin1, R2.Pin_0
  N5: Part2.D2, J2.pin5, Joystick_Left.pin5, Joystick_Left1.pin5, Joystick_Left8.pin1
  N6: Part2.D3, J2.pin6, Joystick_Right.pin1, Joystick_Left2.pin1
  N7: Part2.D4, J2.pin7
  N8: Part2.D5, J2.pin8
  N9: Part2.D6, J2.pin9
  N10: Part2.D7, J2.pin10
  N11: Part2.D8, J2.pin11
  N12: Part2.D9, J2.pin12
  N13: Part2.D10, J2.pin13
  N14: Part2.D11/MOSI, J2.pin14
  N15: Part2.D12/MISO, J2.pin15
  N16: Part2.VIN, J1.pin1, Joystick_Right.pin4, Joystick_Left.pin2, Joystick_Left3.pin1, Joystick_Left1.pin2, Joystick_Left5.pin1, Joystick_Left13.pin1, Joystick_Left14.pin1, R1.Pin_0
  N17: Part2.5V, J1.pin4
  N18: Part2.A7, J1.pin5
  N19: Part2.A6, J1.pin6, Joystick_Right.pin2, Joystick_Left2.pin2, Joystick_Left12.pin1
  N20: Part2.A5, J1.pin7
  N21: Part2.A4, J1.pin8
  N22: Part2.A3, J1.pin9, Joystick_Right.pin3, Joystick_Left2.pin3, Joystick_Left11.pin1
  N23: Part2.A2, J1.pin10, Joystick_Left.pin4, Joystick_Left1.pin4, Joystick_Left7.pin1, Joystick_Left9.pin1
  N24: Part2.A1, J1.pin11, Joystick_Left10.pin1
  N25: Part2.A0, J1.pin12, R1.Pin_1, R2.Pin_1
  N26: Part2.AREF, J1.pin13
  N27: Part2.3V3, J1.pin14
  N28: Part2.D13/SCK, J1.pin15
  N29: Joystick_Left.pin3, Joystick_Left1.pin3, Joystick_Left6.pin1
