# Fritzing sketch joystick_up (saved by Fritzing 0.9.3b)
circuit board: 5.84116cm x 2.40157cm
breadboards: 1

parts:
  Left_connector = female pin header, 15 pins [form="♀ (female)"]
  Right_Connector = female pin header, 15 pins [form="♀ (female)"]
  NRF24 = double row female pin header, 8 pins [form="♀ (female)"]
  NRF26 = female pin header, 4 pins [form="♀ (female)"]
  NRF28 = double row female pin header, 8 pins [form="♀ (female)"]
  R1 = Resistor [tolerance=±5% resistance=4.7k package=THT]
  R3 = Resistor [tolerance=±5% resistance=4.7k package=THT]
  NRF29 = female pin header, 1 pin [form="♀ (female)"]
  NRF30 = female pin header, 1 pin [form="♀ (female)"]
  NRF31 = female pin header, 2 pins [form="♀ (female)"]
  NRF32 = female pin header, 2 pins [form="♀ (female)"]
  NRF33 = female pin header, 1 pin [form="♀ (female)"]

nets:
  N1: Left_connector.pin1, NRF24.pin8, NRF26.pin1
  N2: Left_connector.pin2, NRF24.pin1, NRF24.pin2, NRF29.pin1
  N3: Left_connector.pin3, NRF24.pin6, NRF26.pin3
  N4: Left_connector.pin4, NRF24.pin3, NRF30.pin1
  N5: Left_connector.pin12, NRF24.pin5, NRF26.pin4, NRF28.pin1, NRF28.pin8, R1.Pin_0
  N6: Right_Connector.pin1, NRF24.pin7, NRF26.pin2
  N7: Right_Connector.pin8, NRF28.pin4, NRF28.pin5, NRF31.pin1, NRF32.pin1
  N8: Right_Connector.pin9, NRF28.pin3, NRF28.pin6, NRF31.pin2, NRF32.pin2
  N9: Right_Connector.pin15, NRF28.pin2, NRF28.pin7, R3.Pin_1, NRF33.pin1
  N10: NRF24.pin4, R1.Pin_1, R3.Pin_0

notes:
  4.7k
  2.2k
