# Fritzing sketch joystick_up2 (saved by Fritzing 0.9.3b)
circuit board: 2.5cm x 4cm
breadboards: 1

parts:
  Left_connector = female pin header, 15 pins [form="♀ (female)"]
  Right_Connector = female pin header, 15 pins [form="♀ (female)"]
  NRF24 = double row female pin header, 8 pins [form="♀ (female)"]
  Left_connector2 = female pin header, 2 pins [form="♀ (female)"]
  Left_connector3 = female pin header, 4 pins [form="♀ (female)"]
  Left_connector7 = female pin header, 1 pin [form="♀ (female)"]
  Left_connector8 = female pin header, 1 pin [form="♀ (female)"]
  Left_connector9 = female pin header, 1 pin [form="♀ (female)"]
  Left_connector10 = double row female pin header, 8 pins [form="♀ (female)"]

nets:
  N1: Left_connector.pin1, NRF24.pin4, Left_connector3.pin1, Left_connector8.pin1
  N2: Left_connector.pin2, NRF24.pin6, Left_connector3.pin2, Left_connector9.pin1
  N3: Left_connector.pin3, NRF24.pin2, Left_connector3.pin3
  N4: Left_connector.pin4, NRF24.pin7, Left_connector3.pin4
  N5: Left_connector.pin12, NRF24.pin1, Left_connector2.pin1, Left_connector10.pin4, Left_connector10.pin5
  N6: Right_Connector.pin1, NRF24.pin3, Left_connector7.pin1
  N7: Right_Connector.pin2, NRF24.pin8, Left_connector2.pin2
  N8: Right_Connector.pin8, Left_connector10.pin2, Left_connector10.pin7
  N9: Right_Connector.pin9, Left_connector10.pin1, Left_connector10.pin8
  N10: Right_Connector.pin15, Left_connector10.pin3, Left_connector10.pin6
