# Fritzing sketch joystick_up_bluetooth (saved by Fritzing 0.9.3b)
circuit board: 5.84116cm x 2.40157cm
breadboards: 1

parts:
  Left_connector = female pin header, 15 pins [form="♀ (female)"]
  Right_Connector = female pin header, 15 pins [form="♀ (female)"]
  R1 = Resistor [tolerance=±5% resistance=220 package=THT]
  R2 = Resistor [tolerance=±5% resistance=220 package=THT]
  J1 = female pin header, 6 pins [form="♀ (female)"]
  J2 = female pin header, 6 pins [form="♀ (female)"]
  J3 = female pin header, 2 pins [form="♀ (female)"]
  J4 = female pin header, 2 pins [form="♀ (female)"]

nets:
  N1: Left_connector.pin14, J1.pin3, J2.pin3, J3.pin1
  N2: Left_connector.pin15, J1.pin2, J2.pin2, J3.pin2
  N3: Right_Connector.pin14, J1.pin4, J2.pin4, J4.pin1
  N4: Right_Connector.pin15, R1.Pin_1, R2.Pin_1, J4.pin2
  N5: R2.Pin_0, J1.pin5, J2.pin5
